# Fritzing sketch ASA (saved by Fritzing 0.9.3b)

parts:
  Part2 = Arduino Uno (Rev3) - ICSP
  J2 = Piezo Speaker  # not connected
  YL-83_-_Detection_Board2 = YL-83 Rain Sensor - Detection Board
  YL-83_-_Control_Board2 = YL-83 Rain Sensor - Control Board
  BAT2 = Battery Holders [package=lipo-1100mAh]
  M2 = TP4056 Module [part_number=HW-107]
  OLED_I2C2 = OLED 128x64 I2C Monochrome Display
  SIM800L2 = SIM800L
  DHT2 = DHT11 Humitidy and Temperature Sensor
  S2 = Momentary Switch [package=ksa_sealed_tac_switch]
  R3 = Resistor [tolerance=±5% resistance=100 package="2512 [SMD]"]
  R4 = Resistor [tolerance=±5% resistance=330 package="0805 [SMD]"]  # not connected
  L1 = Inductor [package="400 mil [THT]"]

nets:
  N1: Part2.A0, DHT2.DATA
  N2: Part2.A1, YL-83_-_Control_Board2.AO
  N3: Part2.A4/SDA, OLED_I2C2.SDA
  N4: Part2.A5/SCL, OLED_I2C2.SCK
  N5: Part2.D2, SIM800L2.RXD
  N6: Part2.D3_PWM, SIM800L2.TXD
  N7: Part2.D5_PWM, R3.Pin_0
  N8: Part2.D7, S2.1
  VIN: Part2.VIN, M2.OUT-#4, SIM800L2.VCC
  N9: YL-83_-_Detection_Board2.POS, YL-83_-_Control_Board2.POS
  N10: YL-83_-_Detection_Board2.NEG, YL-83_-_Control_Board2.NEG
  N11: BAT2.+, M2.BAT+
  N12: BAT2.-, M2.BAT-
  N13: M2.OUT-#1, SIM800L2.GND
  N14: SIM800L2.NET, L1.pin_0

custom parts:
  YL-83 Rain Sensor - Detection Board: The YL-83 is a rain sensor that has more resistance when dry and less resistance when wet. The module runs at 5V.
  YL-83 Rain Sensor - Control Board: The YL-83 is a rain sensor that has more resistance when dry and less resistance when wet. The module runs at 5V.
  TP4056 Module: TP4056 Lithium Battery Charge Management Module Links: TP4056 website
  SIM800L: SIM800L is a miniature cellular module which allows for GPRS transmission, sending and receiving SMS and making and receiving voice calls. Low cost and small footprint and quad band frequency support make this module perfect solution for any project that require long range connectivity. After connecting power module boots up, searches for cellular network and login automatically. On board LED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
  DHT11 Humitidy and Temperature Sensor: DHT11 Humidity and Temperature Sensor
